// Logisim project Lab4P2Logisim.circ as structural Verilog: 4 circuits, main circuit main
module main (
  input  in_1,
  input  in_2,
  input  in_3,
  output out_4,
  output out_5
);

  wire and_1_out, nand_1_out, nor_1_out, or_1_out;

  nand nand_1 (nand_1_out, in_1, in_2);
  or or_1 (or_1_out, in_1, in_3);
  and and_1 (and_1_out, nand_1_out, or_1_out);
  nor nor_1 (nor_1_out, nand_1_out, or_1_out);
  not not_1 (out_4, and_1_out);
  not not_2 (out_5, nor_1_out);
endmodule

module Simple (
  input  a,
  input  b,
  input  c,
  output x
);

  wire and_1_out, not_1_out, not_2_out, not_3_out;

  not not_1 (not_1_out, a);
  not not_2 (not_2_out, b);
  and and_1 (and_1_out, not_1_out, not_2_out);
  not not_3 (not_3_out, c);
  or or_1 (x, and_1_out, not_3_out);
endmodule

module ninimalized (
  input  a,
  input  b,
  input  c,
  output x
);

  wire and_1_out, and_2_out, not_1_out, not_2_out;

  not not_1 (not_1_out, a);
  not not_2 (not_2_out, c);
  and and_1 (and_1_out, not_1_out, not_2_out);
  and and_2 (and_2_out, a, b);
  or or_1 (x, and_1_out, and_2_out);
endmodule

module minimal3 (
  input  a,
  input  b,
  input  c,
  output x,
  output y
);

  wire and_1_out, and_2_out, not_1_out, not_2_out;

  not not_1 (not_1_out, a);
  not not_2 (not_2_out, c);
  and and_1 (and_1_out, not_1_out, not_2_out);
  and and_2 (and_2_out, a, b);
  or or_1 (x, and_1_out, and_2_out);

  assign y = 1'b1;
endmodule
